# Fritzing sketch CNY70 (saved by Fritzing 0.9.3b)
breadboards: 1

parts:
  Componente1 = Arduino Mega 2560 (Rev3)
  CNY1 = CNY70
  CNY2 = CNY70
  CNY3 = CNY70
  CNY4 = CNY70
  CNY5 = CNY70
  CNY6 = CNY70
  CNY7 = CNY70
  R1 = Resistor [tolerance=±5% resistance=220 package=THT]
  R2 = Resistor [tolerance=±5% resistance=220 package=THT]
  R3 = Resistor [tolerance=±5% resistance=220 package=THT]
  R4 = Resistor [tolerance=±5% resistance=220 package=THT]
  R5 = Resistor [tolerance=±5% resistance=220 package=THT]
  R6 = Resistor [tolerance=±5% resistance=220 package=THT]
  R7 = Resistor [tolerance=±5% resistance=220 package=THT]

nets:
  N1: Componente1.A0, CNY1.Colector
  N2: Componente1.A1, CNY2.Colector
  N3: Componente1.A2, CNY3.Colector
  N4: Componente1.A3, CNY4.Colector
  N5: Componente1.A4, CNY5.Colector
  N6: Componente1.A5, CNY6.Colector
  N7: Componente1.A6, CNY7.Colector
  N8: CNY1.Anodo, R1.Pin_1
  N9: CNY1.Catodo, CNY2.Catodo, CNY3.Catodo, CNY4.Catodo, CNY5.Catodo, CNY6.Catodo, CNY7.Catodo
  N10: CNY2.Anodo, R2.Pin_1
  N11: CNY3.Anodo, R3.Pin_1
  N12: CNY4.Anodo, R4.Pin_1
  N13: CNY5.Anodo, R5.Pin_1
  N14: CNY6.Anodo, R6.Pin_1
  N15: CNY7.Anodo, R7.Pin_1
  N16: R1.Pin_0, R2.Pin_0, R3.Pin_0, R4.Pin_0, R5.Pin_0, R6.Pin_0, R7.Pin_0

custom parts:
  CNY70: Sensor de Infrarojos de corto alcance.
